# Fritzing sketch Musical Instrument (saved by Fritzing 0.9.3b)
circuit board: 8.46667cm x 5.64444cm
breadboards: 1

parts:
  Part1 = Arduino Uno (Rev3)
  R1 = Resistor [tolerance=±10% resistance=10M package=THT]
  J1 = female pin header, 2 pins [form="♀ (female)"]
  R2 = Resistor [tolerance=±10% resistance=10M package=THT]

nets:
  N1: Part1.D8, R2.Pin_1
  N2: Part1.D2, R1.Pin_0, J1.pin1
  N3: Part1.D4, R1.Pin_1
  N4: Part1.D6_PWM, J1.pin2, R2.Pin_0
