# Fritzing sketch Servor and arduino Sketch (saved by Fritzing 0.9.3b)
circuit board: 8.46667cm x 5.64444cm
breadboards: 1

parts:
  VCC2 = Battery
  Part1 = Arduino Uno (Rev3)
  S1 = Toggle Switch [package=THT]
  VCC1 = Battery
  J1 = Basic Servo
  IC2 = ULN2803A [package=THT]
  M3 = Stepper Motor - Unipolar
  M4 = Stepper Motor - Unipolar

nets:
  N1: VCC2.-, VCC1.+
  N2: VCC2.+, S1.L2
  N3: Part1.D8, J1.pulse
  N4: Part1.D10_PWM/SS, IC2.In_5
  N5: Part1.D11_PWM/MOSI, IC2.In_6
  N6: Part1.D12/MISO, IC2.In_7
  N7: Part1.D13/SCK, IC2.In_8
  GND: Part1.GND, VCC1.-, J1.gnd, IC2.0V, M3.D, M4.D
  N8: Part1.D3_PWM, IC2.In_2
  N9: Part1.D4, IC2.In_3
  N10: Part1.D5_PWM, IC2.In_4
  5V: Part1.5V, S1.COM, J1.vcc, IC2.Out_5, M3.A, M4.A
  N11: IC2.COM_-_Common, M4.COMMON_2
  N12: IC2.Out_8, M4.B
  N13: IC2.Out_7, M4.C
  N14: IC2.Out_6, M4.COMMON_1
  N15: IC2.Out_4, M3.COMMON_2
  N16: IC2.Out_3, M3.B
  N17: IC2.Out_2, M3.C
  N18: IC2.Out_1, M3.COMMON_1
